# Fritzing sketch Схема(генератор случайных чисел) (4) (saved by Fritzing 0.9.10b)

parts:
  M2 = Stepper Motor - Bipolar
  M3 = DC Motor [voltage_(max)=6V voltage_(min)=3V]
  Pololu_A1 = Pololu A4988 [package=SO16]
  Driver1 = 28BYJ-48 Driver Module [part_number=ULN2003 package=THT]
  SM1 = 28BYJ-48 Stepper Motor [part_number=28BYJ-48]
  A1 = MX1508
  J1 = Power Jack [package=power_jack_pth_lock]
  Компонент1 = Arduino Nano (Rev3.0)
  23 = Rasberry Pi NIOR Camera [chip_label=IC package="DIP (Dual Inline) [THT]"]  # not connected
  S2 = Square Pushbutton
  U1 = Nokia 6100 Color LCD [mn=пва package=nokia6100_lcd]  # not connected
  Mod1 = Raspberry Pi 4B  # not connected
  U2 = LM2596 step down module
  X1 = USB Connectors [package=usb-a-s]
  C1 = Capacitor [package=cap-pth-small-kit]
  S3 = Limit Switch [package="Breakout Board"]
  U4 = Sharp PC817 [package=THT]

nets:
  N1: M2.A, Pololu_A1.2B
  N2: M2.C, Pololu_A1.2A
  N3: M2.B, Pololu_A1.1A
  N4: M2.D, Pololu_A1.1B
  N5: M3.pin_1, A1.Pin_8
  N6: M3.pin_2, A1.Pin_7
  GND: Pololu_A1.ENABLE, Pololu_A1.MS1, Pololu_A1.MS2, Pololu_A1.GND, Driver1.GND, A1.Pin_2, J1.GND, Компонент1.GND, U2.IN-, U2.OUT-, X1.GND, C1.2, S3.G, U4.Pin_2, U4.Pin_3
  N7: Pololu_A1.STEP, Компонент1.D7
  N8: Pololu_A1.DIR, Компонент1.D6
  N9: Pololu_A1.VDD, Driver1.Vmotor, U2.OUT+, X1.VBUS
  N10: Pololu_A1.VMOT, A1.Pin_1, S2.leg1, U2.IN+, U4.Pin_1
  N11: Driver1.IN1, Компонент1.D5
  N12: Driver1.IN2, Компонент1.D4
  N13: Driver1.IN3, Компонент1.D3
  N14: Driver1.IN4, Компонент1.D2
  N15: Driver1.blue-pin, SM1.blue-pin
  N16: Driver1.pink-pin, SM1.pink-pin
  N17: Driver1.yellow-pin, SM1.yellow-pin
  N18: Driver1.orange-pin, SM1.orange-pin
  N19: Driver1.red-pin, SM1.red-pin
  N20: A1.Pin_5, Компонент1.D11/MOSI
  N21: A1.Pin_6, Компонент1.D10
  N22: J1.PWR, S2.leg0
  N23: Компонент1.D8, S3.S
  N24: Компонент1.VIN, Компонент1.A0, C1.1, U4.Pin_4
  N25: Компонент1.3V3, S3.V

notes:
  Микромотор с редуктором GA12-N20 Gear Motor подключенный к драйверу MX1508
  Шаговый двигатель 17HE15-1504S поключенный к драйверу TMC2208
  Шаговый двигатель
  28BYJ-48 поключенный к драйверу ULN2003
  Плата Arduino Nano с подключенным разделительным конденсатором(0.1 мкФ)
  Плата Raspberry Pi 4B с питанем через распаянный USB
  камера Raspberry Pi High Quality (OV5647)
  Питание от PowerJack 12V с кнопкой аварийной остановки .
  Питание от PowerJack 12V с кнопкой питания.
  Понижающий преобразователь с USB LM2596S
  Raspberry Pi Дисплей с HDMI подключением, работающий на XPT2046
  Концевик
  Оптопара(Датчик линии)

custom parts:
  28BYJ-48 Driver Module: High-power ULN2003 Stepper Motor Driver Board Test Module For Arduino AVR SMD
  28BYJ-48 Stepper Motor: Unipolar Stepper Motor 28BYJ-48 Top coil - pink & orange Bottom coil - blue & yellow Common rail - red Connector pins: blue - pink - yellow - orange - red
  MX1508: MX1508 DC Motor Driver is a low-cost motor driver module that can control DC stepper motors of current rating up to 2A.
  Rasberry Pi NIOR Camera: Camera
  LM2596 step down module: LM2596 DC-DC step down power supply module 3 A.
  Limit Switch: Generic limit switch commonly found on 3D printers. Typical lever microswitch mounted on a PCB board with a 3 pin JST XH connector.
